# Fritzing sketch pressure_plate_feather_huzzah_ESP (saved by Fritzing 0.9.4)
breadboards: 1

parts:
  Part1 = Adafruit Feather HUZZAH ESP8266 [part_number="Adafruit #2821"]
  NEOPIXEL1 = Neopixel Strip -- Black (30/m) [part_number=1376]
  S1 = Momentary Switch [package=ksa_sealed_tac_switch]
  R1 = Resistor [tolerance=±5% resistance=10k package="2512 [SMD]"]
  C1 = Electrolytic Capacitor [capacitance=22µF voltage=10V package="0605 [SMD, electrolytic]"]

nets:
  GND: Part1.GND, NEOPIXEL1.GND, R1.Pin_1, C1.+
  3.3V: Part1.3.3V, NEOPIXEL1.+5V, S1.4, C1.-
  N1: Part1.GPIO5/SCL, NEOPIXEL1.Din
  N2: Part1.GPIO4/SDA, S1.1
  N3: S1.2, R1.Pin_0

custom parts:
  Adafruit Feather HUZZAH ESP8266: his is the Adafruit Feather HUZZAH ESP8266 - our take on an 'all-in-one' ESP8266 WiFi development board with built in USB and battery charging. Its an ESP8266 WiFi module with all the extras you need, ready to rock! We have other boards in the Feather family, check'em out here. At the Feather HUZZAH's heart is an ESP8266 WiFi microcontroller clocked at 80 MHz and at 3.3V logic. This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
  Neopixel Strip -- Black (30/m): These NeoPixel strips have 30 digitally-addressable pixel LEDs per meter and are very affordable and are only 12.5 mm wide, 10 mm if you remove the strip from the casing.
